// Logisim project task.circ as structural Verilog: 2 circuits, main circuit test
module test (
  input  in_1,
  input  in_2,
  input  in_3,
  input  in_4,
  input  in_5,
  input  in_6,
  output out_7,
  output out_8,
  output out_9,
  output out_10,
  output out_11,
  output out_12,
  output out_13,
  output out_14
);

  wire clock_1_out, clock_2_out, clock_3_out, clock_4_out;

  Clock clock_1 (.out(clock_1_out));
  Clock clock_2 (.out(clock_2_out));
  D_Flip_Flop d_ff_1 (.D(in_1), .clk(clock_1_out), .Q(out_7), .Qn(out_8));  // open: preset, reset
  T_Flip_Flop t_ff_1 (.T(in_4), .clk(clock_2_out), .Q(out_11), .Qn(out_13));  // open: reset, preset
  Clock clock_3 (.out(clock_3_out));
  Clock clock_4 (.out(clock_4_out));
  S_R_Flip_Flop s_r_ff_1 (.S(in_2), .R(in_3), .clk(clock_3_out), .Q(out_9), .Qn(out_10));  // open: reset, preset
  J_K_Flip_Flop j_k_ff_1 (.J(in_5), .K(in_6), .clk(clock_4_out), .Q(out_12), .Qn(out_14));  // open: preset, reset
endmodule

module main (
  input  in_1,
  output out_2,
  output out_3,
  output out_4,
  output out_5
);

  wire and_1_out, and_2_out, and_3_out, clock_1_out, t_ff_1_qn, t_ff_2_qn, t_ff_3_qn;

  Clock clock_1 (.out(clock_1_out));
  and and_1 (and_1_out, t_ff_1_qn, in_1);
  and and_2 (and_2_out, t_ff_2_qn, t_ff_1_qn, in_1);
  and and_3 (and_3_out, t_ff_3_qn, t_ff_2_qn, t_ff_1_qn, in_1);
  T_Flip_Flop t_ff_1 (.T(in_1), .clk(clock_1_out), .Q(out_2), .Qn(t_ff_1_qn));  // open: reset, preset
  T_Flip_Flop t_ff_2 (.T(and_1_out), .clk(clock_1_out), .Q(out_3), .Qn(t_ff_2_qn));  // open: reset, preset
  T_Flip_Flop t_ff_3 (.T(and_2_out), .clk(clock_1_out), .Q(out_4), .Qn(t_ff_3_qn));  // open: reset, preset
  T_Flip_Flop t_ff_4 (.T(and_3_out), .clk(clock_1_out), .Q(out_5));  // open: Qn, reset, preset
  // Probe on {out_5, out_4, out_3, out_2}
  // Probe on {out_5, out_4, out_3, out_2}
endmodule
